// Logisim project Lab_4_Final.circ as structural Verilog: 12 circuits, main circuit Main
module Main (
);

  wire alu_1_overflow, alu_1_zero, and_1_out, and_3_out, Clock, comparator_1_eq, comparator_2_eq,
       comparator_3_eq, DMCntl2, E_M_beq, E_M_jal, ex_mem_1_zero_2, I_E_beq, I_E_jal, Id_Ex_squash,
       If_Id_beq, If_Id_j, If_Id_jal, If_Id_jr, If_Id_squash, M_W_jal, multiplexer_7_out, not_1_out,
       not_2_out, not_3_out, or_2_out, or_3_out, PCSource, stall;
  wire [1:0] addType, DMCntl, RsCntl, RtCntl;
  wire [1:1] or_1_out;
  wire [2:0] execALUctrl, fetchALUctrl, If_IdALUctrl;
  wire [4:0] A, B, controlSignals, CS, Dest, E_M_A, E_M_B, E_M_Control, E_M_Dest, E_M_FetchRegDest,
       execShamt, fetchRegDest, I_E_A, I_E_B, I_E_Control, I_E_Dest, I_E_Dest_t, id_ex_1_regwrite_2, M_W_A,
       M_W_B, M_W_Control, M_W_Dest, multiplexer_8_out, regDest, Shamt, writeAddress;
  wire [5:0] Func, Opcode;
  wire [7:0] bit_extender_3_out;
  wire [15:0] controlunit_1_address, ImmOp;
  wire [25:0] Offset;
  wire [27:0] bit_extender_1_out, shifter_2_out;
  wire [31:0] adder_2_out, Addr, E_M_jalData, ex_mem_1_out_11, execImmediate, fetchImmediate, I_E_aluRes,
       I_E_jalData, I_I_readData2, id_ex_1_out_13, IF_ID_out_6, If_Id_pc, instMemResult, JRdata, JRdataFinal,
       M_W_jalData, memALUresult, multiplexer_5_out, multiplexer_9_out, multiplexer_10_out,
       multiplexer_11_out, multiplexer_12_out, multiplexer_13_out, multiplexer_14_out, PCafter, PCbefore,
       PCIn, readData2, rom_1_data, shifter_1_out, storeData, subtractor_1_out, WBALUresult, WBLWresult,
       writeData;

  not not_1 (not_1_out, stall);
  Register #(.width(32)) register_1 (.D(PCIn), .en(not_1_out), .Q(PCbefore), .clk(Clock));  // open: clr
  assign bit_extender_1_out = {{2{1'b0}}, Offset};  // Bit_Extender bit_extender_1
  Adder #(.width(32)) adder_1 (.a(32'h4), .b(PCbefore), .out(PCafter));  // open: cin, cout
  Clock clock_1 (.out(Clock));
  Shifter #(.width(32)) shifter_1 (.in(fetchImmediate), .\dist (5'b00010), .out(shifter_1_out));
  Shifter #(.width(28)) shifter_2 (.in(bit_extender_1_out), .\dist (5'b00010), .out(shifter_2_out));
  Adder #(.width(32)) adder_2 (.a(PCbefore), .b(shifter_1_out), .out(adder_2_out));  // open: cin, cout
  Comparator #(.width(5)) comparator_1 (.a(A), .b(E_M_FetchRegDest), .eq(comparator_1_eq));  // open: gt, lt
  Multiplexer #(.width(5)) multiplexer_1 (.in0(controlSignals), .in1({5{1'b0}}), .out(CS), .sel(stall));  // open: en
  Multiplexer #(.width(3)) multiplexer_2 (
    .in0(If_IdALUctrl), .in1(3'b000), .out(fetchALUctrl), .sel(stall));  // open: en
  Multiplexer #(.width(5)) multiplexer_3 (.in0(regDest), .in1({5{1'b0}}), .out(fetchRegDest), .sel(stall));  // open: en
  ROM #(.dataWidth(32)) rom_1 (.addr(PCbefore[9:2]), .data(rom_1_data));  // open: sel
  Multiplexer #(.select(3), .width(32)) multiplexer_4 (
    .in0(PCafter), .in1(adder_2_out), .in2({PCafter[31:28], shifter_2_out}), .in4(JRdataFinal), .out(PCIn),
    .sel({If_Id_jr, or_1_out[1], PCSource}));  // open: in3, in5, in6, in7, en
  // Probe on PCIn
  Multiplexer #(.width(32)) multiplexer_5 (
    .in0(rom_1_data), .in1(IF_ID_out_6), .out(multiplexer_5_out), .sel(stall));  // open: en
  // Probe on multiplexer_5_out
  and and_1 (and_1_out, E_M_Control[4], comparator_1_eq);
  IF_ID IF_ID (
    .in_2(multiplexer_5_out), .out_6(IF_ID_out_6), .Clock(Clock), .in_1(PCafter), .out_5(If_Id_pc),
    .zeroSquash(If_Id_squash));
  Comparator #(.width(5)) comparator_2 (.a(A), .b(B), .eq(comparator_2_eq));  // open: gt, lt
  or or_1 (or_1_out[1], If_Id_j, If_Id_jal);
  Multiplexer #(.width(32)) multiplexer_6 (
    .in0(JRdata), .in1(instMemResult), .out(JRdataFinal), .sel(and_1_out));  // open: en
  // Probe on IF_ID_out_6
  // Probe on multiplexer_7_out
  Multiplexer multiplexer_7 (.in0(1'b0), .in1(If_Id_beq), .out(multiplexer_7_out), .sel(comparator_2_eq));  // open: en
  Multiplexer #(.width(5)) multiplexer_8 (
    .in0(writeAddress), .in1({5{1'b1}}), .out(multiplexer_8_out), .sel(M_W_jal));  // open: en
  Multiplexer #(.width(32)) multiplexer_9 (
    .in0(writeData), .in1(M_W_jalData), .out(multiplexer_9_out), .sel(M_W_jal));  // open: en
  // Probe on fetchImmediate
  controlUnit controlunit_1 (
    .AluCtl(If_IdALUctrl), .Address(controlunit_1_address), .Instruction(IF_ID_out_6), .ImmOprnd(ImmOp),
    .Shamt(Shamt), .Des(Dest), .B(B), .A(A), .addType(addType), .OPC(Opcode), .Off(Offset), .Func(Func),
    .controlSignals(controlSignals), .regDest(regDest), .Jump(If_Id_j), .BEQ(If_Id_beq), .JumpReg(If_Id_jr),
    .JumpAndLoad(If_Id_jal));
  not not_2 (not_2_out, stall);
  // Probe on multiplexer_8_out
  // Probe on multiplexer_9_out
  or or_2 (or_2_out, M_W_Control[1], M_W_jal);
  assign fetchImmediate = {{16{1'b0}}, controlunit_1_address};  // Bit_Extender bit_extender_2
  squasher squasher_1 (
    .J(If_Id_j), .beq(multiplexer_7_out), .clk(Clock), .stall(not_2_out), .If_Id_squash(If_Id_squash),
    .Id_Ex_squash(Id_Ex_squash), .JR(If_Id_jr), .JAL(If_Id_jal));
  Register_File register_file_1 (
    .WrAddr(multiplexer_8_out), .WrData(multiplexer_9_out), .WrReg(or_2_out), .RdAddr1(A), .RdAddr2(B),
    .RdData1(JRdata), .RdData2(I_I_readData2), .Clock(not_3_out));
  not not_3 (not_3_out, Clock);
  Subtractor #(.width(32)) subtractor_1 (.a(PCIn), .b(32'h4), .out(subtractor_1_out));  // open: bin, bout
  // Probe on JRdata
  // Probe on I_I_readData2
  // Probe on subtractor_1_out
  ID_EX id_ex_1 (
    .in_1(JRdata), .in_2(I_I_readData2), .in_3(fetchImmediate), .ALUctrl(fetchALUctrl), .controlSignals(CS),
    .regWrite(fetchRegDest), .fetchA(A), .fetchB(B), .fetchShamt(Shamt), .fetchDest(Dest),
    .out_13(id_ex_1_out_13), .out_14(readData2), .out_15(execImmediate), .ALUctrl_2(execALUctrl),
    .controlSignals_2(I_E_Control), .regWrite_2(id_ex_1_regwrite_2), .execA(I_E_A), .execB(I_E_B),
    .execShamt(execShamt), .execDest(I_E_Dest), .CLK(Clock), .pc(If_Id_pc));  // open: pc_2
  Register #(.width(1)) register_2 (.D(If_Id_beq), .Q(I_E_beq), .clk(Clock));  // open: en, clr
  Register #(.width(1)) register_3 (.D(If_Id_jal), .Q(I_E_jal), .clk(Clock));  // open: en, clr
  Register #(.width(32)) register_4 (.D(subtractor_1_out), .Q(I_E_jalData), .clk(Clock));  // open: en, clr
  // Probe on I_E_jalData
  Hazard_Detection_Unit hazard_detection_unit_1 (
    .Id_ExRt(I_E_B), .If_IdRs(A), .Id_ExRd(I_E_Dest_t), .If_IdRt(B), .opCode(Opcode),
    .MemRead(I_E_Control[4]), .stall(stall));
  // Probe on id_ex_1_out_13
  // Probe on I_E_Control
  Multiplexer #(.width(32), .enable("false")) multiplexer_10 (
    .in0(readData2), .in1(execImmediate), .out(multiplexer_10_out), .sel(I_E_Control[2]));
  Multiplexer #(.width(32)) multiplexer_11 (
    .in0(multiplexer_12_out), .in1(M_W_jalData), .out(multiplexer_11_out), .sel(M_W_jal));  // open: en
  Multiplexer #(.select(2), .width(32)) multiplexer_12 (
    .in0(id_ex_1_out_13), .in1(WBALUresult), .in2(WBLWresult), .in3(memALUresult), .out(multiplexer_12_out),
    .sel(RsCntl));  // open: en
  ALU alu_1 (
    .ALUCtl(execALUctrl), .A(multiplexer_11_out), .B(multiplexer_13_out), .ALUResult(I_E_aluRes),
    .Zero(alu_1_zero), .Overflow(alu_1_overflow), .Shamt(execShamt));
  Multiplexer #(.select(2), .width(32)) multiplexer_13 (
    .in0(multiplexer_10_out), .in1(WBALUresult), .in2(WBLWresult), .in3(memALUresult),
    .out(multiplexer_13_out), .sel(RtCntl));  // open: en
  Multiplexer #(.width(32), .enable("false")) multiplexer_14 (
    .in0(readData2), .in1(WBALUresult), .out(multiplexer_14_out), .sel(DMCntl2));
  // Probe on execALUctrl
  // Probe on alu_1_overflow
  // Probe on alu_1_zero
  Forwarding_Unit forwarding_unit_1 (
    .Id_ExType(I_E_Control), .Ex_MemType(E_M_Control), .Mem_WType(M_W_Control), .Id_ExRs(I_E_A),
    .Id_ExRt(I_E_B), .Ex_MemRd(E_M_Dest), .Ex_MemRt(E_M_B), .Mem_WRd(M_W_Dest), .Mem_WRt(M_W_B),
    .DMDataInCntl(DMCntl), .RtCntl(RtCntl), .RsCntl(RsCntl), .ForDataMem(DMCntl2));
  and and_2 (PCSource, ex_mem_1_zero_2, E_M_beq);
  EX_MEM ex_mem_1 (
    .Zero(alu_1_zero), .ALU_Result(I_E_aluRes), .in_3(multiplexer_14_out),
    .in_4({id_ex_1_regwrite_2, I_E_Control}), .Zero_2(ex_mem_1_zero_2), .ALUResult(memALUresult),
    .out_11(ex_mem_1_out_11), .out_12({E_M_FetchRegDest, E_M_Control}), .Clk(Clock), .in_5(I_E_A),
    .out_13(E_M_A), .in_6(I_E_B), .out_14(E_M_B), .in_7(I_E_Dest), .out_15(E_M_Dest));
  Register #(.width(1)) register_5 (.D(I_E_beq), .Q(E_M_beq), .clk(Clock));  // open: en, clr
  Register #(.width(1)) register_6 (.D(I_E_jal), .Q(E_M_jal), .clk(Clock));  // open: en, clr
  Register #(.width(32)) register_7 (.D(I_E_jalData), .Q(E_M_jalData), .clk(Clock));  // open: en, clr
  // Probe on E_M_jalData
  // Probe on bit_extender_3_out
  // Probe on E_M_beq
  Bit_Extender #(.in_width(32), .out_width(8)) bit_extender_3 (.in(Addr), .out(bit_extender_3_out));
  // Probe on DMCntl
  Comparator #(.width(5)) comparator_3 (.a(E_M_FetchRegDest), .b(M_W_B), .eq(comparator_3_eq));  // open: gt, lt
  // Probe on memALUresult
  // Probe on storeData
  Multiplexer #(.select(2), .width(32)) multiplexer_15 (
    .in0(ex_mem_1_out_11), .in1(WBALUresult), .in2(WBLWresult), .out(storeData), .sel(DMCntl));  // open: in3, en
  // Probe on E_M_Control[3]
  and and_3 (and_3_out, E_M_Control[3], comparator_3_eq);
  // Probe on readData2
  RAM #(.dataWidth(32), .bus("separate")) ram_1 (
    .addr(bit_extender_3_out), .din(storeData), .data(instMemResult), .str(E_M_Control[3]), .clk(Clock),
    .ld(E_M_Control[4]));  // open: sel, clr
  // Probe on E_M_Control[4]
  // Probe on Addr
  or or_3 (or_3_out, M_W_jal, and_3_out);
  Multiplexer #(.width(32)) multiplexer_16 (
    .in0(memALUresult), .in1(readData2), .out(Addr), .sel(or_3_out));  // open: en
  // Probe on instMemResult
  // Probe on E_M_FetchRegDest
  MEM_WB mem_wb_1 (
    .ALU_Result(instMemResult), .in_2(memALUresult), .in_3({E_M_FetchRegDest, E_M_Control}),
    .ALUResult(WBLWresult), .out_9(WBALUresult), .out_10({writeAddress, M_W_Control}), .Clk(Clock),
    .in_4(E_M_A), .out_11(M_W_A), .in_5(E_M_B), .out_12(M_W_B), .in_6(E_M_Dest), .out_13(M_W_Dest));
  Register #(.width(1)) register_8 (.D(E_M_jal), .Q(M_W_jal), .clk(Clock));  // open: en, clr
  // Probe on M_W_B
  Register #(.width(32)) register_9 (.D(E_M_jalData), .Q(M_W_jalData), .clk(Clock));  // open: en, clr
  // Probe on WBLWresult
  Multiplexer #(.width(32), .enable("false")) multiplexer_17 (
    .in0(WBALUresult), .in1(WBLWresult), .out(writeData), .sel(M_W_Control[4]));
  // Probe on WBALUresult
  // Probe on M_W_Control[4]

  // Other names for the same wires on the sheet: I_E_MemRead = I_E_Control[4]; writeReg = M_W_Control[1];
  //   memCSandDest[9:0] = {E_M_FetchRegDest, E_M_Control}; E_M_SW = E_M_Control[3]; E_M_LW = E_M_Control[4]

  // Notes on the sheet:
  //   IF_PC[31..0]
  //   contents of rom_1 (hex, n*v repeats v):
  //   34010001 211020 221820 2064000e 232822 aca4000e 8ca6000e c43824 10e10003 c7402a 11080001 201a0001
  //   20090001 8c0a000c ad4a0013 8c0a000c 1141fffb c000013 201b0001 23ff002c ac1f0000 308b0010 456027
  //   446825 97140 27842 8c100000 2000008 201c0001 800001d 201d0001 201e0001
  //   IF_Instruction[31..0]
  //   Hazard Detection Unit
  //   EX/MEM
  //   MEM/WB
  //   ALUresult or Mem?
endmodule

module ALU (
  input  [2:0] ALUCtl,
  input  [31:0] A,
  input  [31:0] B,
  input  [4:0] Shamt,
  output [31:0] ALUResult,
  output Zero,
  output Overflow
);

  wire comparator_1_lt, comparator_2_lt, comparator_3_eq, comparator_4_eq, or_2_out;
  wire [31:0] ADD, AND, NOR, OR, SLL, SLT, SLTU, SRL, SUB, XOR;

  assign XOR = A ^ B;  // XOR_Gate xor_1, 32 bits wide
  Adder #(.width(32)) adder_1 (.a(A), .b(B), .out(ADD));  // open: cin, cout
  Subtractor #(.width(32)) subtractor_1 (.a(A), .b(B), .out(SUB));  // open: bin, bout
  assign AND = A & B;  // AND_Gate and_1, 32 bits wide
  assign OR = A | B;  // OR_Gate or_1, 32 bits wide
  assign NOR = ~(A | B);  // NOR_Gate nor_1, 32 bits wide
  Comparator #(.width(32)) comparator_1 (.a(A), .b(B), .lt(comparator_1_lt));  // open: gt, eq
  assign SLT = {{31{1'b0}}, comparator_1_lt};  // Bit_Extender bit_extender_1
  Shifter #(.width(32)) shifter_1 (.in(B), .\dist (Shamt), .out(SLL));
  Shifter #(.width(32), .shift("lr")) shifter_2 (.in(B), .\dist (Shamt), .out(SRL));
  Comparator #(.width(32), .mode("unsigned")) comparator_2 (.a(A), .b(B), .lt(comparator_2_lt));  // open: gt, eq
  assign SLTU = {{31{1'b0}}, comparator_2_lt};  // Bit_Extender bit_extender_2
  Multiplexer #(.select(3), .width(32), .enable("false")) multiplexer_1 (
    .in0(NOR), .in1(AND), .in2(SUB), .in3(SLT), .in4(OR), .in5(ADD), .in6(SLL), .in7(SRL), .out(ALUResult),
    .sel(ALUCtl));
  Comparator #(.width(3)) comparator_3 (.a(3'b101), .b(ALUCtl), .eq(comparator_3_eq));  // open: gt, lt
  Comparator #(.width(3)) comparator_4 (.a(ALUCtl), .b(3'b010), .eq(comparator_4_eq));  // open: gt, lt
  Overflow_Unit overflow_unit_1 (
    .Add(comparator_3_eq), .Sub(comparator_4_eq), .ASign(A[31]), .BSign(B[31]), .ResultSign(ALUResult[31]),
    .Overflow(Overflow));
  or or_2 (or_2_out, ALUResult[0], ALUResult[1], ALUResult[2], ALUResult[3], ALUResult[4], ALUResult[5], ALUResult[6], ALUResult[7], ALUResult[8], ALUResult[9], ALUResult[10], ALUResult[11], ALUResult[12], ALUResult[13], ALUResult[14], ALUResult[15], ALUResult[16], ALUResult[17], ALUResult[18], ALUResult[19], ALUResult[20], ALUResult[21], ALUResult[22], ALUResult[23], ALUResult[24], ALUResult[25], ALUResult[26], ALUResult[27], ALUResult[28], ALUResult[29], ALUResult[30], ALUResult[31]);
  not not_1 (Zero, or_2_out);

  // Other names for the same wires on the sheet: ASign = A[31]; ResultSign = ALUResult[31]; BSign = B[31]

  // Notes on the sheet:
  //   ALUCtl for ADD on top port
  //   ALUCtl for SUB on second port
endmodule

module Register_File (
  input  [4:0] WrAddr,
  input  [31:0] WrData,
  input  WrReg,
  input  [4:0] RdAddr1,
  input  [4:0] RdAddr2,
  input  Clock,
  output [31:0] RdData1,
  output [31:0] RdData2
);

  wire and_1_out, and_2_out, comparator_1_eq, comparator_2_eq, comparator_3_eq, comparator_4_eq, not_1_out,
       not_2_out, WrReg0, WrReg1, WrReg2, WrReg3, WrReg4, WrReg5, WrReg6, WrReg7, WrReg8, WrReg9, WrReg10,
       WrReg11, WrReg12, WrReg13, WrReg14, WrReg15, WrReg16, WrReg17, WrReg18, WrReg19, WrReg20, WrReg21,
       WrReg22, WrReg23, WrReg24, WrReg25, WrReg26, WrReg27, WrReg28, WrReg29, WrReg30, WrReg31;
  wire [31:0] multiplexer_1_out, multiplexer_2_out, RegData1, RegData2, RegData3, RegData4, RegData5,
       RegData6, RegData7, RegData8, RegData9, RegData10, RegData11, RegData12, RegData13, RegData14,
       RegData15, RegData16, RegData17, RegData18, RegData19, RegData20, RegData21, RegData22, RegData23,
       RegData24, RegData25, RegData26, RegData27, RegData28, RegData29, RegData30, RegData31;

  Demultiplexer #(.select(5), .enable("false")) demultiplexer_1 (
    .out0(WrReg0), .out1(WrReg1), .out2(WrReg2), .out3(WrReg3), .out4(WrReg4), .out5(WrReg5), .out6(WrReg6),
    .out7(WrReg7), .out8(WrReg8), .out9(WrReg9), .out10(WrReg10), .out11(WrReg11), .out12(WrReg12),
    .out13(WrReg13), .out14(WrReg14), .out15(WrReg15), .out16(WrReg16), .out17(WrReg17), .out18(WrReg18),
    .out19(WrReg19), .out20(WrReg20), .out21(WrReg21), .out22(WrReg22), .out23(WrReg23), .out24(WrReg24),
    .out25(WrReg25), .out26(WrReg26), .out27(WrReg27), .out28(WrReg28), .out29(WrReg29), .out30(WrReg30),
    .out31(WrReg31), .in(WrReg), .sel(WrAddr));
  // Probe on RegData4
  Register #(.width(32)) Reg4 (.D(WrData), .en(WrReg4), .Q(RegData4), .clk(Clock));  // open: clr
  // Probe on RegData8
  Register #(.width(32)) Reg8 (.D(WrData), .en(WrReg8), .Q(RegData8), .clk(Clock));  // open: clr
  // Probe on RegData12
  Register #(.width(32)) Reg12 (.D(WrData), .en(WrReg12), .Q(RegData12), .clk(Clock));  // open: clr
  // Probe on RegData16
  Register #(.width(32)) Reg16 (.D(WrData), .en(WrReg16), .Q(RegData16), .clk(Clock));  // open: clr
  // Probe on RegData20
  Register #(.width(32)) Reg20 (.D(WrData), .en(WrReg20), .Q(RegData20), .clk(Clock));  // open: clr
  // Probe on RegData24
  Register #(.width(32)) Reg24 (.D(WrData), .en(WrReg24), .Q(RegData24), .clk(Clock));  // open: clr
  // Probe on RegData28
  Register #(.width(32)) Reg28 (.D(WrData), .en(WrReg28), .Q(RegData28), .clk(Clock));  // open: clr
  Register #(.width(32)) Reg1 (.D(WrData), .en(WrReg1), .Q(RegData1), .clk(Clock));  // open: clr
  Register #(.width(32)) Reg5 (.D(WrData), .en(WrReg5), .Q(RegData5), .clk(Clock));  // open: clr
  Register #(.width(32)) Reg9 (.D(WrData), .en(WrReg9), .Q(RegData9), .clk(Clock));  // open: clr
  Register #(.width(32)) Reg13 (.D(WrData), .en(WrReg13), .Q(RegData13), .clk(Clock));  // open: clr
  Register #(.width(32)) Reg17 (.D(WrData), .en(WrReg17), .Q(RegData17), .clk(Clock));  // open: clr
  Register #(.width(32)) Reg21 (.D(WrData), .en(WrReg21), .Q(RegData21), .clk(Clock));  // open: clr
  Register #(.width(32)) Reg25 (.D(WrData), .en(WrReg25), .Q(RegData25), .clk(Clock));  // open: clr
  Register #(.width(32)) Reg29 (.D(WrData), .en(WrReg29), .Q(RegData29), .clk(Clock));  // open: clr
  // Probe on RegData1
  // Probe on RegData5
  // Probe on RegData9
  // Probe on RegData13
  // Probe on RegData17
  // Probe on RegData21
  // Probe on RegData25
  // Probe on RegData29
  // Probe on RegData2
  Register #(.width(32)) Reg2 (.D(WrData), .en(WrReg2), .Q(RegData2), .clk(Clock));  // open: clr
  // Probe on RegData6
  Register #(.width(32)) Reg6 (.D(WrData), .en(WrReg6), .Q(RegData6), .clk(Clock));  // open: clr
  // Probe on RegData10
  Register #(.width(32)) Reg10 (.D(WrData), .en(WrReg10), .Q(RegData10), .clk(Clock));  // open: clr
  // Probe on RegData14
  Register #(.width(32)) Reg14 (.D(WrData), .en(WrReg14), .Q(RegData14), .clk(Clock));  // open: clr
  // Probe on RegData18
  Register #(.width(32)) Reg18 (.D(WrData), .en(WrReg18), .Q(RegData18), .clk(Clock));  // open: clr
  // Probe on RegData22
  Register #(.width(32)) Reg22 (.D(WrData), .en(WrReg22), .Q(RegData22), .clk(Clock));  // open: clr
  // Probe on RegData26
  Register #(.width(32)) Reg26 (.D(WrData), .en(WrReg26), .Q(RegData26), .clk(Clock));  // open: clr
  // Probe on RegData30
  Register #(.width(32)) Reg30 (.D(WrData), .en(WrReg30), .Q(RegData30), .clk(Clock));  // open: clr
  // Probe on RegData3
  Register #(.width(32)) Reg3 (.D(WrData), .en(WrReg3), .Q(RegData3), .clk(Clock));  // open: clr
  // Probe on RegData7
  Register #(.width(32)) Reg7 (.D(WrData), .en(WrReg7), .Q(RegData7), .clk(Clock));  // open: clr
  // Probe on RegData11
  Register #(.width(32)) Reg11 (.D(WrData), .en(WrReg11), .Q(RegData11), .clk(Clock));  // open: clr
  // Probe on RegData15
  Register #(.width(32)) Reg15 (.D(WrData), .en(WrReg15), .Q(RegData15), .clk(Clock));  // open: clr
  // Probe on RegData19
  Register #(.width(32)) Reg19 (.D(WrData), .en(WrReg19), .Q(RegData19), .clk(Clock));  // open: clr
  // Probe on RegData23
  Register #(.width(32)) Reg23 (.D(WrData), .en(WrReg23), .Q(RegData23), .clk(Clock));  // open: clr
  // Probe on RegData27
  Register #(.width(32)) Reg27 (.D(WrData), .en(WrReg27), .Q(RegData27), .clk(Clock));  // open: clr
  // Probe on RegData31
  Register #(.width(32)) Reg31 (.D(WrData), .en(WrReg31), .Q(RegData31), .clk(Clock));  // open: clr
  Multiplexer #(.select(5), .width(32), .enable("false")) multiplexer_1 (
    .in0({32{1'b0}}), .in1(RegData1), .in2(RegData2), .in3(RegData3), .in4(RegData4), .in5(RegData5),
    .in6(RegData6), .in7(RegData7), .in8(RegData8), .in9(RegData9), .in10(RegData10), .in11(RegData11),
    .in12(RegData12), .in13(RegData13), .in14(RegData14), .in15(RegData15), .in16(RegData16),
    .in17(RegData17), .in18(RegData18), .in19(RegData19), .in20(RegData20), .in21(RegData21),
    .in22(RegData22), .in23(RegData23), .in24(RegData24), .in25(RegData25), .in26(RegData26),
    .in27(RegData27), .in28(RegData28), .in29(RegData29), .in30(RegData30), .in31(RegData31),
    .out(multiplexer_1_out), .sel(RdAddr1));
  Multiplexer #(.select(5), .width(32), .enable("false")) multiplexer_2 (
    .in0({32{1'b0}}), .in1(RegData1), .in2(RegData2), .in3(RegData3), .in4(RegData4), .in5(RegData5),
    .in6(RegData6), .in7(RegData7), .in8(RegData8), .in9(RegData9), .in10(RegData10), .in11(RegData11),
    .in12(RegData12), .in13(RegData13), .in14(RegData14), .in15(RegData15), .in16(RegData16),
    .in17(RegData17), .in18(RegData18), .in19(RegData19), .in20(RegData20), .in21(RegData21),
    .in22(RegData22), .in23(RegData23), .in24(RegData24), .in25(RegData25), .in26(RegData26),
    .in27(RegData27), .in28(RegData28), .in29(RegData29), .in30(RegData30), .in31(RegData31),
    .out(multiplexer_2_out), .sel(RdAddr2));
  Multiplexer #(.width(32), .enable("false")) multiplexer_3 (
    .in0(multiplexer_1_out), .in1(WrData), .out(RdData1), .sel(and_1_out));
  Comparator #(.width(5), .mode("unsigned")) comparator_1 (
    .a(WrAddr), .b(RdAddr2), .eq(comparator_1_eq));  // open: gt, lt
  Multiplexer #(.width(32), .enable("false")) multiplexer_4 (
    .in0(multiplexer_2_out), .in1(WrData), .out(RdData2), .sel(and_2_out));
  Comparator #(.width(5), .mode("unsigned")) comparator_2 (
    .a(WrAddr), .b(RdAddr1), .eq(comparator_2_eq));  // open: gt, lt
  and and_1 (and_1_out, comparator_2_eq, WrReg, not_1_out);
  and and_2 (and_2_out, comparator_1_eq, WrReg, not_2_out);
  Comparator #(.width(5), .mode("unsigned")) comparator_3 (
    .a(WrAddr), .b({5{1'b0}}), .eq(comparator_3_eq));  // open: gt, lt
  not not_1 (not_1_out, comparator_3_eq);
  Comparator #(.width(5), .mode("unsigned")) comparator_4 (
    .a(WrAddr), .b({5{1'b0}}), .eq(comparator_4_eq));  // open: gt, lt
  not not_2 (not_2_out, comparator_4_eq);
endmodule

module Overflow_Unit (
  input  Add,
  input  Sub,
  input  ASign,
  input  BSign,
  input  ResultSign,
  output Overflow
);

  wire and_1_out, and_2_out, or_1_out, xnor_1_out, xor_1_out, xor_2_out;

  xnor xnor_1 (xnor_1_out, ASign, BSign);
  xor xor_1 (xor_1_out, ASign, BSign);
  and and_1 (and_1_out, xnor_1_out, Add);
  and and_2 (and_2_out, xor_1_out, Sub);
  or or_1 (or_1_out, and_1_out, and_2_out);
  xor xor_2 (xor_2_out, ResultSign, ASign);
  and and_3 (Overflow, or_1_out, xor_2_out);

  // Notes on the sheet:
  //   Overflow occurs when doing addition and sign(A) == sign(B) && sign(result) != sign(A)
  //   Or
  //   Overflow occurs when doing subtraction and sign(A) != sign(B) && sign(result) != sign(A)
endmodule

module IF_ID (
  input  [31:0] in_1,
  input  [31:0] in_2,
  input  zeroSquash,
  input  Clock,
  output [31:0] out_5,
  output [31:0] out_6
);

  Register #(.width(32)) register_1 (.D(in_1), .Q(out_5), .clk(Clock));  // open: en, clr
  Register #(.width(32)) register_2 (.D(in_2), .Q(out_6), .clk(Clock), .clr(zeroSquash));  // open: en
endmodule

module ID_EX (
  input  [31:0] in_1,
  input  [31:0] in_2,
  input  [31:0] in_3,
  input  [2:0] ALUctrl,
  input  [4:0] controlSignals,
  input  [4:0] regWrite,
  input  [4:0] fetchA,
  input  [4:0] fetchB,
  input  [4:0] fetchShamt,
  input  [4:0] fetchDest,
  input  [31:0] pc,
  input  CLK,
  output [31:0] out_13,
  output [31:0] out_14,
  output [31:0] out_15,
  output [2:0] ALUctrl_2,
  output [4:0] controlSignals_2,
  output [4:0] regWrite_2,
  output [4:0] execA,
  output [4:0] execB,
  output [4:0] execShamt,
  output [4:0] execDest,
  output [31:0] pc_2
);

  Register #(.width(32)) register_1 (.D(in_1), .Q(out_13), .clk(CLK));  // open: en, clr
  Register #(.width(32)) register_2 (.D(in_2), .Q(out_14), .clk(CLK));  // open: en, clr
  Register #(.width(32)) register_3 (.D(in_3), .Q(out_15), .clk(CLK));  // open: en, clr
  Register #(.width(3)) register_4 (.D(ALUctrl), .Q(ALUctrl_2), .clk(CLK));  // open: en, clr
  Register #(.width(5)) register_5 (.D(controlSignals), .Q(controlSignals_2), .clk(CLK));  // open: en, clr
  Register #(.width(5)) register_6 (.D(regWrite), .Q(regWrite_2), .clk(CLK));  // open: en, clr
  Register #(.width(5)) register_7 (.D(fetchA), .Q(execA), .clk(CLK));  // open: en, clr
  Register #(.width(5)) register_8 (.D(fetchB), .Q(execB), .clk(CLK));  // open: en, clr
  Register #(.width(5)) register_9 (.D(fetchShamt), .Q(execShamt), .clk(CLK));  // open: en, clr
  Register #(.width(5)) register_10 (.D(fetchDest), .Q(execDest), .clk(CLK));  // open: en, clr
  Register #(.width(32)) register_11 (.D(pc), .Q(pc_2), .clk(CLK));  // open: en, clr
endmodule

module EX_MEM (
  input  Zero,
  input  [31:0] ALU_Result,
  input  [31:0] in_3,
  input  [9:0] in_4,
  input  [4:0] in_5,
  input  [4:0] in_6,
  input  [4:0] in_7,
  input  Clk,
  output Zero_2,
  output [31:0] ALUResult,
  output [31:0] out_11,
  output [9:0] out_12,
  output [4:0] out_13,
  output [4:0] out_14,
  output [4:0] out_15
);

  Register #(.width(10)) register_1 (.D(in_4), .Q(out_12), .clk(Clk));  // open: en, clr
  Register #(.width(5)) register_2 (.D(in_5), .Q(out_13), .clk(Clk));  // open: en, clr
  Register #(.width(5)) register_3 (.D(in_6), .Q(out_14), .clk(Clk));  // open: en, clr
  Register #(.width(5)) register_4 (.D(in_7), .Q(out_15), .clk(Clk));  // open: en, clr
  Register #(.width(1)) register_5 (.D(Zero), .Q(Zero_2), .clk(Clk));  // open: en, clr
  Register #(.width(32)) register_6 (.D(ALU_Result), .Q(ALUResult), .clk(Clk));  // open: en, clr
  Register #(.width(32)) register_7 (.D(in_3), .Q(out_11), .clk(Clk));  // open: en, clr
endmodule

module MEM_WB (
  input  [31:0] ALU_Result,
  input  [31:0] in_2,
  input  [9:0] in_3,
  input  [4:0] in_4,
  input  [4:0] in_5,
  input  [4:0] in_6,
  input  Clk,
  output [31:0] ALUResult,
  output [31:0] out_9,
  output [9:0] out_10,
  output [4:0] out_11,
  output [4:0] out_12,
  output [4:0] out_13
);

  Register #(.width(32)) register_1 (.D(ALU_Result), .Q(ALUResult), .clk(Clk));  // open: en, clr
  Register #(.width(32)) register_2 (.D(in_2), .Q(out_9), .clk(Clk));  // open: en, clr
  Register #(.width(10)) register_3 (.D(in_3), .Q(out_10), .clk(Clk));  // open: en, clr
  Register #(.width(5)) register_4 (.D(in_4), .Q(out_11), .clk(Clk));  // open: en, clr
  Register #(.width(5)) register_5 (.D(in_5), .Q(out_12), .clk(Clk));  // open: en, clr
  Register #(.width(5)) register_6 (.D(in_6), .Q(out_13), .clk(Clk));  // open: en, clr
endmodule

// Control Unit
module controlUnit (
  input  [31:0] Instruction,
  output [2:0] AluCtl,
  output [15:0] Address,
  output [15:0] ImmOprnd,
  output [4:0] Shamt,
  output [4:0] Des,
  output [4:0] B,
  output [4:0] A,
  output [1:0] addType,
  output [5:0] Func,
  output [5:0] OPC,
  output [25:0] Off,
  output JumpAndLoad,
  output JumpReg,
  output Jump,
  output BEQ,
  output [4:0] controlSignals,
  output [4:0] regDest
);

  wire Add, Addi, And, and_1_out, and_2_out, Andi, Clock, EX_MEM_beq, EX_MEM_jump, FuncSel, ID_EX_beq,
       ID_EX_jump, IF_ID_beq, IF_ID_jump, isImmediate, isShift, JR, Nor, Or, or_2_out, or_3_out, Ori,
       Rformat, SLL, SLT, SRL, Sub;

  // Probe on Instruction[15:0]
  // Probe on Instruction[15:0]
  Decoder #(.select(5)) decoder_1 (
    .out0(FuncSel), .out2(Jump), .out3(JumpAndLoad), .out4(BEQ), .out8(Addi), .out12(Andi), .out13(Ori),
    .out19(controlSignals[4]), .out27(controlSignals[3]), .sel({Instruction[31], Instruction[29:26]}));  // open: out1, out5, out6, out7, out9, out10, out11, out14, out15, out16, out17, out18, out20, out21, out22, out23, out24, out25, out26, out28, out29, out30, out31, en
  ROM #(.addrWidth(10), .dataWidth(3)) rom_1 (
    .addr({Instruction[31], Instruction[29:26], Instruction[5], Instruction[3:0]}), .data(AluCtl));  // open: sel
  Decoder #(.select(5)) decoder_2 (
    .out0(SLL), .out2(SRL), .out8(JR), .out16(Add), .out18(Sub), .out20(And), .out21(Or), .out23(Nor),
    .out26(SLT), .sel({Instruction[5], Instruction[3:0]}));  // open: out1, out3, out4, out5, out6, out7, out9, out10, out11, out12, out13, out14, out15, out17, out19, out22, out24, out25, out27, out28, out29, out30, out31, en
  and and_1 (and_1_out, ~Instruction[31], ~Instruction[30], ~Instruction[29], ~Instruction[28], ~Instruction[27], ~Instruction[26]);  // AND_Gate
  and and_2 (and_2_out, ~Instruction[5], ~Instruction[4], Instruction[3], ~Instruction[2], ~Instruction[1], ~Instruction[0]);  // AND_Gate
  and and_3 (JumpReg, and_1_out, and_2_out);
  or or_1 (isImmediate, Addi, Andi, Ori);
  Register #(.width(1)) register_1 (.D(IF_ID_beq), .Q(ID_EX_beq), .clk(Clock));  // open: en, clr
  Register #(.width(1)) register_2 (.D(IF_ID_jump), .Q(ID_EX_jump), .clk(Clock));  // open: en, clr
  or or_2 (or_2_out, SLL, SRL);
  or or_3 (or_3_out, Add, Sub, And, Or, Nor, SLT);
  or or_4 (controlSignals[2], controlSignals[3], controlSignals[4], isImmediate);
  and and_4 (isShift, or_2_out, FuncSel);
  or or_5 (controlSignals[0], isImmediate, controlSignals[3], controlSignals[4]);
  or or_6 (controlSignals[1], isShift, controlSignals[4], Rformat, isImmediate);
  and and_5 (Rformat, or_3_out, FuncSel);
  Multiplexer #(.width(5), .enable("false")) multiplexer_1 (
    .in0(Instruction[15:11]), .in1(Instruction[20:16]), .out(regDest), .sel(controlSignals[0]));
  Register #(.width(1)) register_3 (.D(ID_EX_beq), .Q(EX_MEM_beq), .clk(Clock));  // open: en, clr
  Register #(.width(1)) register_4 (.D(ID_EX_jump), .Q(EX_MEM_jump), .clk(Clock));  // open: en, clr

  assign A = Instruction[25:21];
  assign Address = Instruction[15:0];
  assign addType = {Instruction[31], Instruction[29]};
  assign B = Instruction[20:16];
  assign Des = Instruction[15:11];
  assign Func = Instruction[5:0];
  assign ImmOprnd = Instruction[15:0];
  assign Off = Instruction[25:0];
  assign OPC = Instruction[31:26];
  assign Shamt = Instruction[10:6];

  // Other names for the same wires on the sheet: SW = controlSignals[3]; LW = controlSignals[4];
  //   Offset[25:0] = Instruction[25:0]; dest[4:0] = Instruction[15:11]; J = Jump; JAL = JumpAndLoad;
  //   toAlu[2:0] = AluCtl

  // Notes on the sheet:
  //   contents of rom_1 (hex, n*v repeats v):
  //   6 0 7 5*0 5 0 0 0 1 4 0 0 5 0 2 0 1 4 4*0 3 229*0 32*5 96*0 32*1 32*4 160*0 32*5 224*0 32*5
  //   destIsB??
endmodule

module Forwarding_Unit (
  input  [4:0] Id_ExType,
  input  [4:0] Ex_MemType,
  input  [4:0] Mem_WType,
  input  [4:0] Id_ExRs,
  input  [4:0] Id_ExRt,
  input  [4:0] Ex_MemRd,
  input  [4:0] Ex_MemRt,
  input  [4:0] Mem_WRd,
  input  [4:0] Mem_WRt,
  output [1:0] DMDataInCntl,
  output [1:0] RtCntl,
  output [1:0] RsCntl,
  output ForDataMem
);

  wire and_1_out, and_2_out, and_3_out, and_4_out, and_5_out, and_6_out, and_7_out, and_8_out, and_9_out,
       and_10_out, and_11_out, and_12_out, and_13_out, and_14_out, and_16_out, and_17_out, and_18_out,
       and_19_out, and_20_out, and_21_out, and_22_out, and_23_out, and_25_out, and_26_out, and_27_out,
       and_28_out, and_29_out, and_31_out, and_32_out, and_33_out, and_34_out, and_35_out, and_36_out,
       and_37_out, and_38_out, and_39_out, and_40_out, and_41_out, and_42_out, and_43_out, and_44_out,
       and_46_out, and_47_out, and_49_out, and_50_out, and_51_out, and_52_out, and_53_out, and_54_out,
       and_56_out, and_57_out, and_58_out, and_59_out, and_60_out, and_61_out, and_62_out, and_63_out,
       and_64_out, and_65_out, and_66_out, and_67_out, and_68_out, and_69_out, and_70_out, and_71_out,
       and_72_out, and_73_out, and_74_out, and_75_out, and_76_out, and_77_out, and_78_out, and_79_out,
       and_80_out, and_81_out, and_82_out, and_83_out, and_84_out, and_85_out, comparator_1_eq,
       comparator_2_eq, comparator_3_eq, comparator_4_eq, comparator_5_eq, comparator_6_eq, comparator_7_eq,
       comparator_8_eq, comparator_9_eq, comparator_10_eq, comparator_11_eq, comparator_12_eq,
       comparator_13_eq, comparator_14_eq, comparator_15_eq, comparator_16_eq, comparator_17_eq,
       comparator_18_eq, comparator_19_eq, comparator_20_eq, comparator_21_eq, comparator_22_eq,
       comparator_23_eq, comparator_24_eq, comparator_25_eq, comparator_26_eq, comparator_27_eq,
       comparator_28_eq, comparator_29_eq, comparator_30_eq, comparator_31_eq, comparator_32_eq,
       comparator_33_eq, comparator_34_eq, Ex_MemI, Ex_MemR_Sh, Id_ExLW_SW, LW_to_Rs, LW_to_Rt, M_W_LW,
       Mem_WI, Mem_WR_Sh, not_1_out, not_2_out, not_3_out, not_4_out, or_1_out, or_2_out, or_5_out, or_7_out,
       or_8_out, or_11_out, or_13_out, or_15_out, WB_ALU_to_Rs, WB_ALU_to_Rt;

  Comparator #(.width(5)) comparator_1 (.a({5{1'b0}}), .b(Mem_WRd), .eq(comparator_1_eq));  // open: gt, lt
  Comparator #(.width(5)) comparator_2 (.a({5{1'b0}}), .b(Mem_WRd), .eq(comparator_2_eq));  // open: gt, lt
  and and_1 (and_1_out, Ex_MemType[0], ~Ex_MemType[1], Ex_MemType[2], Ex_MemType[3], ~Ex_MemType[4]);  // AND_Gate
  and and_2 (and_2_out, Mem_WType[0], Mem_WType[1], ~Mem_WType[2], ~Mem_WType[3], ~Mem_WType[4]);  // AND_Gate
  or or_1 (or_1_out, and_2_out, and_3_out);
  and and_3 (and_3_out, ~Mem_WType[0], Mem_WType[1], ~Mem_WType[2], ~Mem_WType[3], ~Mem_WType[4]);  // AND_Gate
  not not_1 (not_1_out, comparator_1_eq);
  Comparator #(.width(5)) comparator_3 (.a(Mem_WRd), .b(Ex_MemRt), .eq(comparator_3_eq));  // open: gt, lt
  and and_4 (and_4_out, Ex_MemType[0], ~Ex_MemType[1], Ex_MemType[2], Ex_MemType[3], ~Ex_MemType[4]);  // AND_Gate
  and and_5 (and_5_out, Mem_WType[0], Mem_WType[1], Mem_WType[2], ~Mem_WType[3], ~Mem_WType[4]);  // AND_Gate
  Comparator #(.width(5)) comparator_4 (.a(Mem_WRt), .b(Ex_MemRt), .eq(comparator_4_eq));  // open: gt, lt
  and and_6 (and_6_out, Ex_MemType[0], ~Ex_MemType[1], Ex_MemType[2], Ex_MemType[3], ~Ex_MemType[4]);  // AND_Gate
  and and_7 (and_7_out, Mem_WType[0], Mem_WType[1], Mem_WType[2], ~Mem_WType[3], Mem_WType[4]);  // AND_Gate
  Comparator #(.width(5)) comparator_5 (.a(Mem_WRt), .b(Ex_MemRt), .eq(comparator_5_eq));  // open: gt, lt
  and and_8 (and_8_out, Id_ExType[0], ~Id_ExType[1], Id_ExType[2], Id_ExType[3], ~Id_ExType[4]);  // AND_Gate
  and and_9 (and_9_out, Mem_WType[0], Mem_WType[1], ~Mem_WType[2], ~Mem_WType[3], ~Mem_WType[4]);  // AND_Gate
  and and_10 (and_10_out, ~Mem_WType[0], Mem_WType[1], ~Mem_WType[2], ~Mem_WType[3], ~Mem_WType[4]);  // AND_Gate
  not not_2 (not_2_out, comparator_2_eq);
  Comparator #(.width(5)) comparator_6 (.a(Mem_WRd), .b(Id_ExRt), .eq(comparator_6_eq));  // open: gt, lt
  and and_11 (and_11_out, Id_ExType[0], ~Id_ExType[1], Id_ExType[2], Id_ExType[3], ~Id_ExType[4]);  // AND_Gate
  and and_12 (and_12_out, Mem_WType[0], Mem_WType[1], Mem_WType[2], ~Mem_WType[3], ~Mem_WType[4]);  // AND_Gate
  Comparator #(.width(5)) comparator_7 (.a(Mem_WRt), .b(Id_ExRt), .eq(comparator_7_eq));  // open: gt, lt
  and and_13 (and_13_out, or_1_out, not_1_out);
  and and_14 (and_14_out, and_4_out, and_5_out, comparator_4_eq);
  and and_15 (DMDataInCntl[1], and_6_out, and_7_out, comparator_5_eq);
  or or_2 (or_2_out, and_9_out, and_10_out);
  and and_16 (and_16_out, or_2_out, not_2_out);
  and and_17 (and_17_out, and_11_out, and_12_out, comparator_7_eq);
  and and_18 (and_18_out, and_1_out, and_13_out, comparator_3_eq);
  and and_19 (and_19_out, and_8_out, and_16_out, comparator_6_eq);
  // Probe on DMDataInCntl
  or or_3 (DMDataInCntl[0], and_18_out, and_14_out);
  or or_4 (ForDataMem, and_19_out, and_17_out);
  Comparator #(.width(5)) comparator_8 (.a({5{1'b0}}), .b(Ex_MemRd), .eq(comparator_8_eq));  // open: gt, lt
  and and_20 (and_20_out, Id_ExType[0], Id_ExType[1], Id_ExType[2], ~Id_ExType[3], ~Id_ExType[4]);  // AND_Gate
  Comparator #(.width(5)) comparator_9 (.a({5{1'b0}}), .b(Mem_WRd), .eq(comparator_9_eq));  // open: gt, lt
  and and_21 (and_21_out, Id_ExType[0], ~Id_ExType[1], Id_ExType[2], Id_ExType[3], ~Id_ExType[4]);  // AND_Gate
  and and_22 (and_22_out, Ex_MemType[0], Ex_MemType[1], Ex_MemType[2], ~Ex_MemType[3], Ex_MemType[4]);  // AND_Gate
  Comparator #(.width(5)) comparator_10 (.a(Ex_MemRt), .b(Id_ExRs), .eq(comparator_10_eq));  // open: gt, lt
  and and_23 (and_23_out, ~Id_ExType[0], Id_ExType[1], ~Id_ExType[2], ~Id_ExType[3], ~Id_ExType[4]);  // AND_Gate
  and and_24 (M_W_LW, Mem_WType[0], Mem_WType[1], Mem_WType[2], ~Mem_WType[3], Mem_WType[4]);  // AND_Gate
  Comparator #(.width(5)) comparator_11 (.a(Mem_WRt), .b(Id_ExRs), .eq(comparator_11_eq));  // open: gt, lt
  and and_25 (and_25_out, Id_ExType[0], Id_ExType[1], Id_ExType[2], ~Id_ExType[3], ~Id_ExType[4]);  // AND_Gate
  Comparator #(.width(5)) comparator_12 (.a(Mem_WRt), .b(Id_ExRs), .eq(comparator_12_eq));  // open: gt, lt
  and and_26 (and_26_out, Id_ExType[0], Id_ExType[1], Id_ExType[2], ~Id_ExType[3], ~Id_ExType[4]);  // AND_Gate
  Comparator #(.width(5)) comparator_13 (.a(Ex_MemRd), .b(Id_ExRs), .eq(comparator_13_eq));  // open: gt, lt
  and and_27 (and_27_out, Ex_MemType[0], Ex_MemType[1], ~Ex_MemType[2], ~Ex_MemType[3], ~Ex_MemType[4]);  // AND_Gate
  and and_28 (and_28_out, ~Ex_MemType[0], Ex_MemType[1], ~Ex_MemType[2], ~Ex_MemType[3], ~Ex_MemType[4]);  // AND_Gate
  not not_3 (not_3_out, comparator_8_eq);
  Comparator #(.width(5)) comparator_14 (.a(Ex_MemRd), .b(Id_ExRs), .eq(comparator_14_eq));  // open: gt, lt
  and and_29 (and_29_out, ~Id_ExType[0], Id_ExType[1], ~Id_ExType[2], ~Id_ExType[3], ~Id_ExType[4]);  // AND_Gate
  Comparator #(.width(5)) comparator_15 (.a(Ex_MemRt), .b(Id_ExRs), .eq(comparator_15_eq));  // open: gt, lt
  and and_30 (Ex_MemI, Ex_MemType[0], Ex_MemType[1], Ex_MemType[2], ~Ex_MemType[3], ~Ex_MemType[4]);  // AND_Gate
  Comparator #(.width(5)) comparator_16 (.a(Ex_MemRt), .b(Id_ExRs), .eq(comparator_16_eq));  // open: gt, lt
  and and_31 (and_31_out, ~Id_ExType[0], Id_ExType[1], ~Id_ExType[2], ~Id_ExType[3], ~Id_ExType[4]);  // AND_Gate
  and and_32 (and_32_out, Id_ExType[0], Id_ExType[1], Id_ExType[2], ~Id_ExType[3], Id_ExType[4]);  // AND_Gate
  and and_33 (and_33_out, Id_ExType[0], ~Id_ExType[1], Id_ExType[2], Id_ExType[3], ~Id_ExType[4]);  // AND_Gate
  and and_34 (and_34_out, Ex_MemType[0], Ex_MemType[1], ~Ex_MemType[2], ~Ex_MemType[3], ~Ex_MemType[4]);  // AND_Gate
  and and_35 (and_35_out, ~Ex_MemType[0], Ex_MemType[1], ~Ex_MemType[2], ~Ex_MemType[3], ~Ex_MemType[4]);  // AND_Gate
  Comparator #(.width(5)) comparator_17 (.a(Ex_MemRd), .b(Id_ExRs), .eq(comparator_17_eq));  // open: gt, lt
  and and_36 (and_36_out, Ex_MemType[0], Ex_MemType[1], Ex_MemType[2], ~Ex_MemType[3], ~Ex_MemType[4]);  // AND_Gate
  Comparator #(.width(5)) comparator_18 (.a(Ex_MemRt), .b(Id_ExRs), .eq(comparator_18_eq));  // open: gt, lt
  and and_37 (and_37_out, Id_ExType[0], Id_ExType[1], Id_ExType[2], ~Id_ExType[3], ~Id_ExType[4]);  // AND_Gate
  Comparator #(.width(5)) comparator_19 (.a(Mem_WRd), .b(Id_ExRs), .eq(comparator_19_eq));  // open: gt, lt
  and and_38 (and_38_out, Mem_WType[0], Mem_WType[1], ~Mem_WType[2], ~Mem_WType[3], ~Mem_WType[4]);  // AND_Gate
  and and_39 (and_39_out, ~Mem_WType[0], Mem_WType[1], ~Mem_WType[2], ~Mem_WType[3], ~Mem_WType[4]);  // AND_Gate
  not not_4 (not_4_out, comparator_9_eq);
  Comparator #(.width(5)) comparator_20 (.a(Mem_WRd), .b(Id_ExRs), .eq(comparator_20_eq));  // open: gt, lt
  and and_40 (and_40_out, ~Id_ExType[0], Id_ExType[1], ~Id_ExType[2], ~Id_ExType[3], ~Id_ExType[4]);  // AND_Gate
  and and_41 (and_41_out, Id_ExType[0], Id_ExType[1], Id_ExType[2], ~Id_ExType[3], ~Id_ExType[4]);  // AND_Gate
  Comparator #(.width(5)) comparator_21 (.a(Mem_WRt), .b(Id_ExRs), .eq(comparator_21_eq));  // open: gt, lt
  and and_42 (and_42_out, ~Id_ExType[0], Id_ExType[1], ~Id_ExType[2], ~Id_ExType[3], ~Id_ExType[4]);  // AND_Gate
  and and_43 (and_43_out, and_21_out, and_22_out, comparator_10_eq);
  and and_44 (and_44_out, and_25_out, M_W_LW, comparator_12_eq);
  or or_5 (or_5_out, and_27_out, and_28_out);
  and and_45 (Ex_MemR_Sh, or_5_out, not_3_out);
  and and_46 (and_46_out, and_20_out, Ex_MemI, comparator_15_eq);
  or or_6 (Id_ExLW_SW, and_32_out, and_33_out);
  or or_7 (or_7_out, and_34_out, and_35_out);
  and and_47 (and_47_out, Id_ExLW_SW, and_36_out, comparator_18_eq);
  or or_8 (or_8_out, and_38_out, and_39_out);
  and and_48 (Mem_WI, Mem_WType[0], Mem_WType[1], Mem_WType[2], ~Mem_WType[3], ~Mem_WType[4]);  // AND_Gate
  Comparator #(.width(5)) comparator_22 (.a(Mem_WRt), .b(Id_ExRs), .eq(comparator_22_eq));  // open: gt, lt
  and and_49 (and_49_out, and_23_out, M_W_LW, comparator_11_eq);
  and and_50 (and_50_out, and_26_out, Ex_MemR_Sh, comparator_13_eq);
  and and_51 (and_51_out, Ex_MemR_Sh, comparator_14_eq, and_29_out);
  and and_52 (and_52_out, Ex_MemI, comparator_16_eq, and_31_out);
  and and_53 (and_53_out, Id_ExLW_SW, or_7_out, comparator_17_eq);
  and and_54 (and_54_out, and_37_out, Mem_WR_Sh, comparator_19_eq);
  and and_55 (Mem_WR_Sh, or_8_out, not_4_out);
  and and_56 (and_56_out, Mem_WR_Sh, comparator_20_eq, and_40_out);
  and and_57 (and_57_out, and_41_out, Mem_WI, comparator_21_eq);
  and and_58 (and_58_out, Mem_WI, comparator_22_eq, and_42_out);
  or or_9 (LW_to_Rs, and_43_out, and_49_out, and_44_out);
  or or_10 (WB_ALU_to_Rs, and_54_out, and_56_out, and_57_out, and_58_out);
  or or_11 (or_11_out, and_50_out, and_51_out, and_46_out, and_52_out, and_53_out, and_47_out);
  Multiplexer #(.width(2)) multiplexer_1 (
    .in0({LW_to_Rs, WB_ALU_to_Rs}), .in1(2'b11), .out(RsCntl), .sel(or_11_out));  // open: en
  and and_59 (and_59_out, ~Id_ExType[0], Id_ExType[1], ~Id_ExType[2], ~Id_ExType[3], ~Id_ExType[4]);  // AND_Gate
  Comparator #(.width(5)) comparator_23 (.a(Mem_WRt), .b(Id_ExRt), .eq(comparator_23_eq));  // open: gt, lt
  and and_60 (and_60_out, Id_ExType[0], Id_ExType[1], ~Id_ExType[2], ~Id_ExType[3], ~Id_ExType[4]);  // AND_Gate
  Comparator #(.width(5)) comparator_24 (.a(Mem_WRt), .b(Id_ExRt), .eq(comparator_24_eq));  // open: gt, lt
  and and_61 (and_61_out, Id_ExType[0], Id_ExType[1], ~Id_ExType[2], ~Id_ExType[3], ~Id_ExType[4]);  // AND_Gate
  Comparator #(.width(5)) comparator_25 (.a(Ex_MemRd), .b(Id_ExRt), .eq(comparator_25_eq));  // open: gt, lt
  and and_62 (and_62_out, ~Id_ExType[0], Id_ExType[1], ~Id_ExType[2], ~Id_ExType[3], ~Id_ExType[4]);  // AND_Gate
  Comparator #(.width(5)) comparator_26 (.a(Ex_MemRd), .b(Id_ExRt), .eq(comparator_26_eq));  // open: gt, lt
  and and_63 (and_63_out, Id_ExType[0], Id_ExType[1], ~Id_ExType[2], ~Id_ExType[3], ~Id_ExType[4]);  // AND_Gate
  Comparator #(.width(5)) comparator_27 (.a(Ex_MemRt), .b(Id_ExRt), .eq(comparator_27_eq));  // open: gt, lt
  and and_64 (and_64_out, ~Id_ExType[0], Id_ExType[1], ~Id_ExType[2], ~Id_ExType[3], ~Id_ExType[4]);  // AND_Gate
  Comparator #(.width(5)) comparator_28 (.a(Ex_MemRt), .b(Id_ExRt), .eq(comparator_28_eq));  // open: gt, lt
  and and_65 (and_65_out, Id_ExType[0], Id_ExType[1], Id_ExType[2], ~Id_ExType[3], Id_ExType[4]);  // AND_Gate
  and and_66 (and_66_out, Id_ExType[0], ~Id_ExType[1], Id_ExType[2], Id_ExType[3], ~Id_ExType[4]);  // AND_Gate
  and and_67 (and_67_out, Mem_WType[0], Mem_WType[1], ~Mem_WType[2], ~Mem_WType[3], ~Mem_WType[4]);  // AND_Gate
  and and_68 (and_68_out, ~Mem_WType[0], Mem_WType[1], ~Mem_WType[2], ~Mem_WType[3], ~Mem_WType[4]);  // AND_Gate
  Comparator #(.width(5)) comparator_29 (.a(Mem_WRd), .b(Id_ExRs), .eq(comparator_29_eq));  // open: gt, lt
  Comparator #(.width(5)) comparator_30 (.a(Mem_WRt), .b(Id_ExRs), .eq(comparator_30_eq));  // open: gt, lt
  and and_69 (and_69_out, Id_ExType[0], Id_ExType[1], ~Id_ExType[2], ~Id_ExType[3], ~Id_ExType[4]);  // AND_Gate
  Comparator #(.width(5)) comparator_31 (.a(Mem_WRd), .b(Id_ExRt), .eq(comparator_31_eq));  // open: gt, lt
  and and_70 (and_70_out, ~Id_ExType[0], Id_ExType[1], ~Id_ExType[2], ~Id_ExType[3], ~Id_ExType[4]);  // AND_Gate
  Comparator #(.width(5)) comparator_32 (.a(Mem_WRd), .b(Id_ExRt), .eq(comparator_32_eq));  // open: gt, lt
  and and_71 (and_71_out, Id_ExType[0], Id_ExType[1], ~Id_ExType[2], ~Id_ExType[3], ~Id_ExType[4]);  // AND_Gate
  Comparator #(.width(5)) comparator_33 (.a(Mem_WRt), .b(Id_ExRt), .eq(comparator_33_eq));  // open: gt, lt
  and and_72 (and_72_out, ~Id_ExType[0], Id_ExType[1], ~Id_ExType[2], ~Id_ExType[3], ~Id_ExType[4]);  // AND_Gate
  Comparator #(.width(5)) comparator_34 (.a(Mem_WRt), .b(Id_ExRt), .eq(comparator_34_eq));  // open: gt, lt
  and and_73 (and_73_out, and_59_out, M_W_LW, comparator_23_eq);
  and and_74 (and_74_out, and_60_out, M_W_LW, comparator_24_eq);
  or or_12 (Id_ExLW_SW, and_65_out, and_66_out);
  or or_13 (or_13_out, and_67_out, and_68_out);
  and and_75 (and_75_out, Mem_WType[0], Mem_WType[1], Mem_WType[2], ~Mem_WType[3], ~Mem_WType[4]);  // AND_Gate
  or or_14 (LW_to_Rt, and_73_out, and_74_out);
  and and_76 (and_76_out, and_61_out, Ex_MemR_Sh, comparator_25_eq);
  and and_77 (and_77_out, and_62_out, Ex_MemR_Sh, comparator_26_eq);
  and and_78 (and_78_out, and_63_out, Ex_MemI, comparator_27_eq);
  and and_79 (and_79_out, and_64_out, Ex_MemI, comparator_28_eq);
  and and_80 (and_80_out, Id_ExLW_SW, or_13_out, comparator_29_eq);
  and and_81 (and_81_out, Id_ExLW_SW, and_75_out, comparator_30_eq);
  and and_82 (and_82_out, and_69_out, Mem_WR_Sh, comparator_31_eq);
  and and_83 (and_83_out, and_70_out, Mem_WR_Sh, comparator_32_eq);
  and and_84 (and_84_out, and_71_out, Mem_WI, comparator_33_eq);
  and and_85 (and_85_out, and_72_out, Mem_WI, comparator_34_eq);
  or or_15 (or_15_out, and_76_out, and_77_out, and_78_out, and_79_out, and_80_out, and_81_out);
  or or_16 (WB_ALU_to_Rt, and_82_out, and_83_out, and_84_out, and_85_out);
  Multiplexer #(.width(2)) multiplexer_2 (
    .in0({LW_to_Rt, WB_ALU_to_Rt}), .in1(2'b11), .out(RtCntl), .sel(or_15_out));  // open: en

  // Notes on the sheet:
  //   MEM/WB ALU Result to DM Data In Forwarding
  //   Mem/WB Load Result to DM Data In  Forwarding
  //   Rs
  //   WB LW Result to Rs
  //   WB ALU Result to Rs
  //   Mem ALU Result to Rs
  //   Mem ALU Result to Rt
  //   Rt
  //   WB LW Result to Rt
  //   WB ALU Result to Rt
endmodule

module Hazard_Detection_Unit (
  input  [4:0] Id_ExRt,
  input  [4:0] If_IdRs,
  input  [4:0] Id_ExRd,
  input  [4:0] If_IdRt,
  input  [5:0] opCode,
  input  MemRead,
  output stall
);

  wire and_1_out, comparator_1_eq, comparator_2_eq, comparator_3_eq, comparator_4_eq, comparator_5_eq,
       or_1_out, or_2_out, or_3_out;

  Comparator #(.width(6), .mode("unsigned")) comparator_1 (
    .a(opCode), .b(6'b101011), .eq(comparator_1_eq));  // open: gt, lt
  Comparator #(.width(5)) comparator_2 (.a(If_IdRs), .b(Id_ExRd), .eq(comparator_2_eq));  // open: gt, lt
  Comparator #(.width(5)) comparator_3 (.a(Id_ExRd), .b(If_IdRt), .eq(comparator_3_eq));  // open: gt, lt
  Comparator #(.width(5)) comparator_4 (.a(If_IdRs), .b(Id_ExRt), .eq(comparator_4_eq));  // open: gt, lt
  Comparator #(.width(5)) comparator_5 (.a(Id_ExRt), .b(If_IdRt), .eq(comparator_5_eq));  // open: gt, lt
  or or_1 (or_1_out, comparator_2_eq, comparator_3_eq);
  or or_2 (or_2_out, comparator_4_eq, comparator_5_eq);
  or or_3 (or_3_out, or_2_out, or_1_out);
  and and_1 (and_1_out, or_3_out, ~comparator_1_eq);  // AND_Gate
  and and_2 (stall, and_1_out, MemRead);
endmodule

module squasher (
  input  JR,
  input  JAL,
  input  J,
  input  beq,
  input  clk,
  input  stall,
  output If_Id_squash,
  output Id_Ex_squash
);

  wire or_1_out, register_1_q, register_2_q, register_3_q, register_4_q;

  Register #(.width(1)) register_1 (.D(JR), .en(stall), .Q(register_1_q), .clk(clk), .clr(register_1_q));
  Register #(.width(1)) register_2 (.D(JAL), .en(stall), .Q(register_2_q), .clk(clk), .clr(register_2_q));
  Register #(.width(1)) register_3 (.D(J), .en(stall), .Q(register_3_q), .clk(clk), .clr(register_3_q));
  Register #(.width(1)) register_4 (.D(beq), .en(stall), .Q(register_4_q), .clk(clk), .clr(register_4_q));
  or or_1 (or_1_out, register_1_q, register_3_q, register_4_q, register_2_q);
  and and_1 (If_Id_squash, or_1_out, stall);
  and and_2 (Id_Ex_squash, or_1_out, stall);
endmodule
